// Logisim project real ai alu.circ as structural Verilog
module in_a_and_in_b (
  input  [7:0] in_1,
  input  [7:0] in_2,
  output z,
  output [7:0] out_4
);

  assign out_4 = in_1 & in_2;  // AND_Gate and_1, 8 bits wide
  nor nor_1 (z, out_4[0], out_4[1], out_4[2], out_4[3], out_4[4], out_4[5], out_4[6], out_4[7]);
endmodule

module in_a_or_in_b (
  input  [7:0] in_1,
  input  [7:0] in_2,
  output [7:0] out_3,
  output z
);

  assign out_3 = in_1 | in_2;  // OR_Gate or_1, 8 bits wide
  nor nor_1 (z, out_3[0], out_3[1], out_3[2], out_3[3], out_3[4], out_3[5], out_3[6], out_3[7]);
endmodule

module not_in_b (
  input  [7:0] in_1,
  output [7:0] out_2,
  output z
);

  assign out_2 = ~in_1;  // NOT_Gate not_1, 8 bits wide
  nor nor_1 (z, out_2[0], out_2[1], out_2[2], out_2[3], out_2[4], out_2[5], out_2[6], out_2[7]);
endmodule

module LSL_in_b (
  input  [7:0] in_1,
  output z,
  output n,
  output c,
  output [7:0] out_5
);

  nor nor_1 (z, 1'b0, in_1[0], in_1[1], in_1[2], in_1[3], in_1[4], in_1[5], in_1[6]);

  assign c = in_1[7];
  assign n = in_1[6];
  assign out_5 = {in_1[6:0], 1'b0};
endmodule

module LSR_IN_B (
  input  [7:0] in_1,
  output z,
  output c,
  output n,
  output [7:0] out_5
);

  nor nor_1 (z, in_1[1], in_1[2], in_1[3], in_1[4], in_1[5], in_1[6], in_1[7], 1'b0);

  assign c = in_1[0];
  assign n = 1'b0;
  assign out_5 = {1'b0, in_1[7:1]};
endmodule

module Logic_Circuit (
  input  [7:0] B,
  input  [7:0] A,
  output [7:0] out_3,
  output out_4,
  output out_5,
  output out_6,
  output [7:0] out_7,
  output out_8,
  output out_9,
  output out_10,
  output [7:0] out_11,
  output out_12,
  output [7:0] out_13,
  output out_14,
  output [7:0] out_15,
  output out_16
);

  LSL_in_b lsl_in_b_1 (.in_1(B), .c(out_6), .out_5(out_3), .n(out_4), .z(out_5));
  LSR_IN_B lsr_in_b_1 (.c(out_9), .in_1(B), .z(out_10), .n(out_8), .out_5(out_7));
  in_a_and_in_b in_a_and_in_b_1 (.in_1(B), .in_2(A), .z(out_12), .out_4(out_11));
  in_a_or_in_b in_a_or_in_b_1 (.in_1(A), .in_2(B), .out_3(out_13), .z(out_14));
  not_in_b not_in_b_1 (.in_1(B), .out_2(out_15), .z(out_16));
endmodule

module mux (
  input  in_1,
  input  in_2,
  input  in_3,
  input  in_4,
  input  in_5,
  input  in_6,
  input  in_7,
  input  in_8,
  output out_9
);

  wire and_1_out, and_2_out, and_3_out, and_4_out, and_5_out, not_1_out, not_2_out, not_3_out, not_4_out,
       not_5_out, not_6_out, not_7_out, not_8_out, not_9_out;

  not not_1 (not_1_out, in_2);
  not not_2 (not_2_out, in_2);
  not not_3 (not_3_out, in_3);
  not not_4 (not_4_out, in_2);
  not not_5 (not_5_out, in_1);
  not not_6 (not_6_out, in_3);
  not not_7 (not_7_out, in_1);
  not not_8 (not_8_out, in_1);
  not not_9 (not_9_out, in_3);
  and and_1 (and_1_out, not_5_out, not_1_out, not_6_out, in_4);
  and and_2 (and_2_out, in_5, not_7_out, not_2_out, in_3);
  and and_3 (and_3_out, in_6, not_3_out, in_2, not_8_out);
  and and_4 (and_4_out, in_3, in_2, in_7, not_8_out);
  and and_5 (and_5_out, in_1, not_4_out, not_9_out, in_8);
  or or_1 (out_9, and_1_out, and_2_out, and_3_out, and_4_out, and_5_out);
endmodule
